// Logisim project Whak-a-Mole.circ as structural Verilog: 9 circuits, main circuit main
module main (
  input  [1:0] in_1
);

  wire and_1_out, and_2_out, and_3_out, and_4_out, anti_cheat_1_out_3, anti_cheat_2_1_o1,
       anticlicker_1_out_6, button_1_out, button_2_out, button_3_out, button_4_out, display_1_o1,
       display_1_o2, display_1_o3, display_1_o4, display_1_o5, display_1_o6, display_1_o7, display_1_o8,
       or_1_out, or_2_out, or_3_out, or_4_out, or_5_out, or_6_out, or_7_out, randomiser_1_out_8,
       randomiser_1_out_9, randomiser_1_out_10, randomiser_1_out_11;
  wire [3:0] counter_1_q;

  randomiser randomiser_1 (
    .in_1(counter_1_q), .l1(in_1[0]), .l2(in_1[1]), .in_4(button_1_out), .in_5(button_3_out),
    .in_6(button_4_out), .in_7(button_2_out), .out_8(randomiser_1_out_8), .out_9(randomiser_1_out_9),
    .out_10(randomiser_1_out_10), .out_11(randomiser_1_out_11));
  LED led_1 (.in(randomiser_1_out_8));
  LED led_2 (.in(randomiser_1_out_9));
  LED led_3 (.in(randomiser_1_out_10));
  LED led_4 (.in(randomiser_1_out_11));
  Button button_1 (.out(button_1_out));
  Button button_2 (.out(button_2_out));
  Button button_3 (.out(button_3_out));
  Button button_4 (.out(button_4_out));
  or or_1 (or_1_out, randomiser_1_out_8, randomiser_1_out_9, randomiser_1_out_11, randomiser_1_out_10);
  or or_2 (or_2_out, button_1_out, button_2_out, button_3_out, button_4_out);
  or or_3 (or_3_out, button_1_out, randomiser_1_out_8);
  and and_1 (and_1_out, button_1_out, randomiser_1_out_8);
  or or_4 (or_4_out, button_2_out, randomiser_1_out_9);
  and and_2 (and_2_out, button_2_out, randomiser_1_out_9);
  and and_3 (and_3_out, randomiser_1_out_10, button_3_out);
  or or_5 (or_5_out, randomiser_1_out_10, button_3_out);
  and and_4 (and_4_out, randomiser_1_out_11, button_4_out);
  or or_6 (or_6_out, randomiser_1_out_11, button_4_out);
  anti_cheat anti_cheat_1 (.in_1(or_1_out), .in_2(or_2_out), .out_3(anti_cheat_1_out_3));
  anti_cheat_2 anti_cheat_2_1 (.i1(or_3_out), .i2(or_4_out), .i3(or_5_out), .i4(or_6_out), .o1(anti_cheat_2_1_o1));
  or or_7 (or_7_out, anti_cheat_1_out_3, anti_cheat_2_1_o1);
  anticlicker anticlicker_1 (
    .in_1(or_1_out), .in_2(and_1_out), .in_3(and_2_out), .in_4(and_3_out), .in_5(and_4_out),
    .out_6(anticlicker_1_out_6));
  display display_1 (
    .in_1(counter_1_q), .o1(display_1_o1), .o2(display_1_o2), .o3(display_1_o3), .o4(display_1_o4),
    .o5(display_1_o5), .o6(display_1_o6), .o7(display_1_o7), .o8(display_1_o8));
  Counter #(.width(4), .max('hf)) counter_1 (
    .Q(counter_1_q), .clk(anticlicker_1_out_6), .clr(or_7_out));  // open: load, D, count, carry
  _7_Segment_Display u_7_segment_display_1 (.b(display_1_o8), .c(display_1_o8));  // open: g, f, a, e, d, dp
  _7_Segment_Display u_7_segment_display_2 (
    .g(display_1_o1), .f(display_1_o2), .a(display_1_o4), .b(display_1_o3), .e(display_1_o5),
    .d(display_1_o6), .c(display_1_o7));  // open: dp

  // Notes on the sheet:
  //   INDEX
  //   00 - AUTO LEVEL
  //   01 - EASY
  //   10 - MEDIUM
  //   11 - HARD
endmodule

module memory (
  input  l1,
  input  l2,
  input  [3:0] in_3,
  input  in_4,
  input  in_5,
  input  in_6,
  input  in_7,
  output out_8,
  output out_9,
  output out_10,
  output out_11
);

  wire and_1_out, and_2_out, and_3_out, and_4_out, and_5_out, and_6_out, and_7_out, clock_1_out, clock_2_out,
       clock_3_out, clock_4_out, clock_5_out, clock_6_out, clock_7_out, d_ff_1_q, d_ff_2_q, d_ff_3_q,
       d_ff_4_q, level_selector_1_o1, level_selector_1_o2, level_selector_1_o3, not_1_out, not_2_out,
       not_3_out, not_4_out, or_1_out;

  level_selector level_selector_1 (
    .l1(l1), .l2(l2), .in_3(in_3), .o1(level_selector_1_o1), .o2(level_selector_1_o2),
    .o3(level_selector_1_o3));
  Clock #(.highDuration(16), .lowDuration(16)) clock_1 (.out(clock_1_out));
  not not_1 (not_1_out, or_1_out);
  not not_2 (not_2_out, or_1_out);
  not not_3 (not_3_out, or_1_out);
  not not_4 (not_4_out, or_1_out);
  and and_1 (and_1_out, level_selector_1_o3, clock_1_out);
  Clock clock_2 (.out(clock_2_out));
  Clock clock_3 (.out(clock_3_out));
  Clock clock_4 (.out(clock_4_out));
  Clock clock_5 (.out(clock_5_out));
  Clock #(.highDuration(32), .lowDuration(32)) clock_6 (.out(clock_6_out));
  and and_2 (and_2_out, clock_2_out, not_1_out);
  and and_3 (and_3_out, clock_3_out, not_2_out);
  and and_4 (and_4_out, clock_4_out, not_3_out);
  and and_5 (and_5_out, clock_5_out, not_4_out);
  and and_6 (and_6_out, level_selector_1_o2, clock_6_out);
  D_Flip_Flop d_ff_1 (.clk(and_2_out), .D(in_4), .Q(d_ff_1_q));  // open: Qn, preset, en, reset
  D_Flip_Flop d_ff_2 (.clk(and_3_out), .D(in_5), .Q(d_ff_2_q));  // open: Qn, preset, en, reset
  D_Flip_Flop d_ff_3 (.clk(and_4_out), .D(in_6), .Q(d_ff_3_q));  // open: Qn, preset, en, reset
  D_Flip_Flop d_ff_4 (.clk(and_5_out), .D(in_7), .Q(d_ff_4_q));  // open: Qn, preset, en, reset
  Clock #(.highDuration(64), .lowDuration(64)) clock_7 (.out(clock_7_out));
  or or_1 (or_1_out, and_1_out, and_6_out, and_7_out);
  and and_7 (and_7_out, level_selector_1_o1, clock_7_out);
  and and_8 (out_8, or_1_out, d_ff_1_q);
  and and_9 (out_9, or_1_out, d_ff_2_q);
  and and_10 (out_10, or_1_out, d_ff_3_q);
  and and_11 (out_11, or_1_out, d_ff_4_q);
endmodule

module randomiser (
  input  [3:0] in_1,
  input  l1,
  input  l2,
  input  in_4,
  input  in_5,
  input  in_6,
  input  in_7,
  output out_8,
  output out_9,
  output out_10,
  output out_11
);

  wire and_1_out, clock_1_out, demultiplexer_1_out0, demultiplexer_1_out1, demultiplexer_1_out2,
       demultiplexer_1_out3, or_1_out;
  wire [1:0] counter_1_q;

  or or_1 (or_1_out, in_4, in_5, in_6, in_7);
  Clock clock_1 (.out(clock_1_out));
  and and_1 (and_1_out, or_1_out, clock_1_out);
  Counter #(.width(2), .max('h3)) counter_1 (
    .count(1'b1), .Q(counter_1_q), .clk(and_1_out));  // open: load, D, carry, clr
  Demultiplexer #(.select(2)) demultiplexer_1 (
    .out0(demultiplexer_1_out0), .out1(demultiplexer_1_out1), .out2(demultiplexer_1_out2),
    .out3(demultiplexer_1_out3), .in(1'b1), .sel(counter_1_q));  // open: en
  memory memory_1 (
    .l1(l1), .l2(l2), .in_3(in_1), .in_4(demultiplexer_1_out0), .in_5(demultiplexer_1_out1),
    .in_6(demultiplexer_1_out2), .in_7(demultiplexer_1_out3), .out_8(out_8), .out_9(out_9), .out_10(out_10),
    .out_11(out_11));
endmodule

module level_till_16 (
  input  i1,
  input  i2,
  input  i3,
  input  i4,
  output o1,
  output o2,
  output o3
);

  wire and_1_out, and_2_out, and_3_out, and_4_out, and_5_out, and_6_out, and_7_out, not_1_out, not_2_out,
       not_3_out, not_4_out, not_5_out, not_6_out, not_7_out, not_8_out, not_9_out;

  not not_1 (not_1_out, i1);
  and and_1 (and_1_out, not_1_out, not_2_out);
  not not_2 (not_2_out, i2);
  not not_3 (not_3_out, i1);
  and and_2 (and_2_out, not_3_out, not_4_out, not_5_out);
  not not_4 (not_4_out, i3);
  not not_5 (not_5_out, i4);
  not not_6 (not_6_out, i1);
  and and_3 (and_3_out, not_6_out, i2, i4);
  not not_7 (not_7_out, i1);
  and and_4 (and_4_out, not_7_out, i2, i3);
  and and_5 (and_5_out, i1, not_8_out, not_9_out);
  not not_8 (not_8_out, i2);
  not not_9 (not_9_out, i3);
  and and_6 (and_6_out, i1, i3);
  and and_7 (and_7_out, i1, i2);
  or or_1 (o1, and_1_out, and_2_out);
  or or_2 (o2, and_3_out, and_4_out, and_5_out);
  or or_3 (o3, and_6_out, and_7_out);
endmodule

module level_selector (
  input  l1,
  input  l2,
  input  [3:0] in_3,
  output o1,
  output o2,
  output o3
);

  wire and_1_out, and_2_out, and_3_out, and_4_out, and_5_out, and_6_out, and_7_out, and_8_out, and_9_out,
       and_10_out, not_1_out, not_2_out, not_3_out, not_4_out, not_5_out, not_6_out, not_7_out, not_8_out,
       not_9_out, not_10_out, not_11_out, not_12_out, not_13_out, not_14_out, not_15_out, not_16_out,
       not_17_out, not_18_out, not_19_out, not_20_out;

  not not_1 (not_1_out, l1);
  not not_2 (not_2_out, in_3[3]);
  not not_3 (not_3_out, in_3[2]);
  not not_4 (not_4_out, l1);
  not not_5 (not_5_out, in_3[3]);
  not not_6 (not_6_out, in_3[1]);
  not not_7 (not_7_out, l1);
  not not_8 (not_8_out, l2);
  not not_9 (not_9_out, in_3[3]);
  not not_10 (not_10_out, l2);
  not not_11 (not_11_out, in_3[2]);
  not not_12 (not_12_out, in_3[1]);
  not not_13 (not_13_out, l2);
  not not_14 (not_14_out, in_3[2]);
  not not_15 (not_15_out, in_3[0]);
  not not_16 (not_16_out, l2);
  not not_17 (not_17_out, l1);
  not not_18 (not_18_out, l2);
  not not_19 (not_19_out, l1);
  not not_20 (not_20_out, l2);
  and and_1 (and_1_out, not_1_out, not_2_out, not_3_out);
  and and_2 (and_2_out, not_4_out, not_5_out, not_6_out);
  and and_3 (and_3_out, not_7_out, l2);
  and and_4 (and_4_out, not_8_out, not_9_out, in_3[2], in_3[1]);
  and and_5 (and_5_out, not_10_out, in_3[3], not_11_out, not_12_out);
  and and_6 (and_6_out, not_13_out, in_3[3], not_14_out, not_15_out);
  and and_7 (and_7_out, l1, not_16_out);
  and and_8 (and_8_out, not_17_out, not_18_out, in_3[3], in_3[1], in_3[0]);
  and and_9 (and_9_out, not_19_out, not_20_out, in_3[3], in_3[2]);
  and and_10 (and_10_out, l1, l2);
  or or_1 (o1, and_1_out, and_2_out, and_3_out);
  or or_2 (o2, and_4_out, and_5_out, and_6_out, and_7_out);
  or or_3 (o3, and_8_out, and_9_out, and_10_out);
endmodule

module display (
  input  [3:0] in_1,
  output o1,
  output o2,
  output o3,
  output o4,
  output o5,
  output o6,
  output o7,
  output o8
);

  wire and_1_out, and_2_out, and_3_out, and_4_out, and_5_out, and_6_out, and_7_out, and_8_out, and_9_out,
       and_10_out, and_11_out, and_12_out, and_13_out, and_14_out, and_15_out, and_16_out, and_17_out,
       and_18_out, and_19_out, and_20_out, and_21_out, and_22_out, and_23_out, and_24_out, and_25_out,
       and_26_out, and_27_out, and_28_out, and_29_out, and_30_out, and_31_out, and_32_out, and_33_out,
       not_1_out, not_2_out, not_3_out, not_4_out, not_5_out, not_6_out, not_7_out, not_8_out, not_9_out,
       not_10_out, not_11_out, not_12_out, not_13_out, not_14_out, not_15_out, not_16_out, not_17_out,
       not_18_out, not_19_out, not_20_out, not_21_out, not_22_out, not_23_out, not_24_out, not_25_out,
       not_26_out, not_27_out, not_28_out, not_29_out, not_30_out, not_31_out, not_32_out, not_33_out,
       not_34_out, not_35_out, not_36_out, not_37_out, not_38_out, not_39_out, not_40_out, not_41_out,
       not_42_out, not_43_out, not_44_out;

  not not_1 (not_1_out, in_1[3]);
  not not_2 (not_2_out, in_1[2]);
  not not_3 (not_3_out, in_1[1]);
  not not_4 (not_4_out, in_1[0]);
  not not_5 (not_5_out, in_1[1]);
  not not_6 (not_6_out, in_1[3]);
  not not_7 (not_7_out, in_1[1]);
  not not_8 (not_8_out, in_1[0]);
  not not_9 (not_9_out, in_1[3]);
  not not_10 (not_10_out, in_1[1]);
  not not_11 (not_11_out, in_1[3]);
  not not_12 (not_12_out, in_1[0]);
  not not_13 (not_13_out, in_1[2]);
  not not_14 (not_14_out, in_1[1]);
  not not_15 (not_15_out, in_1[2]);
  not not_16 (not_16_out, in_1[0]);
  not not_17 (not_17_out, in_1[1]);
  not not_18 (not_18_out, in_1[0]);
  not not_19 (not_19_out, in_1[3]);
  not not_20 (not_20_out, in_1[1]);
  not not_21 (not_21_out, in_1[0]);
  not not_22 (not_22_out, in_1[2]);
  not not_23 (not_23_out, in_1[0]);
  not not_24 (not_24_out, in_1[3]);
  not not_25 (not_25_out, in_1[1]);
  not not_26 (not_26_out, in_1[2]);
  not not_27 (not_27_out, in_1[0]);
  not not_28 (not_28_out, in_1[3]);
  not not_29 (not_29_out, in_1[0]);
  not not_30 (not_30_out, in_1[1]);
  not not_31 (not_31_out, in_1[0]);
  not not_32 (not_32_out, in_1[2]);
  not not_33 (not_33_out, in_1[0]);
  not not_34 (not_34_out, in_1[3]);
  not not_35 (not_35_out, in_1[2]);
  not not_36 (not_36_out, in_1[3]);
  not not_37 (not_37_out, in_1[0]);
  not not_38 (not_38_out, in_1[1]);
  not not_39 (not_39_out, in_1[1]);
  not not_40 (not_40_out, in_1[0]);
  not not_41 (not_41_out, in_1[3]);
  not not_42 (not_42_out, in_1[1]);
  not not_43 (not_43_out, in_1[2]);
  and and_1 (and_1_out, in_1[3], in_1[1]);
  and and_2 (and_2_out, in_1[3], in_1[2]);
  and and_3 (and_3_out, not_1_out, not_2_out, in_1[1]);
  and and_4 (and_4_out, in_1[2], not_3_out);
  and and_5 (and_5_out, in_1[2], not_4_out);
  and and_6 (and_6_out, in_1[3], not_5_out);
  and and_7 (and_7_out, in_1[3], in_1[2]);
  and and_8 (and_8_out, not_6_out, not_7_out, not_8_out);
  and and_9 (and_9_out, not_9_out, in_1[2], not_10_out);
  and and_10 (and_10_out, not_11_out, in_1[2], not_12_out);
  and and_11 (and_11_out, in_1[3], not_13_out, not_14_out);
  and and_12 (and_12_out, in_1[3], not_15_out, not_16_out);
  and and_13 (and_13_out, in_1[3], in_1[2], in_1[1]);
  not not_44 (not_44_out, in_1[2]);
  and and_14 (and_14_out, not_17_out, not_18_out);
  and and_15 (and_15_out, not_19_out, in_1[1], in_1[0]);
  and and_16 (and_16_out, in_1[3], not_20_out);
  and and_17 (and_17_out, in_1[3], not_21_out);
  and and_18 (and_18_out, not_22_out, not_23_out);
  and and_19 (and_19_out, not_24_out, in_1[1]);
  and and_20 (and_20_out, in_1[2], in_1[0]);
  and and_21 (and_21_out, in_1[3], not_25_out);
  and and_22 (and_22_out, not_26_out, not_27_out);
  and and_23 (and_23_out, not_28_out, in_1[1], not_29_out);
  and and_24 (and_24_out, in_1[3], not_30_out, not_31_out);
  and and_25 (and_25_out, not_32_out, not_33_out);
  and and_26 (and_26_out, not_34_out, not_35_out, in_1[1]);
  and and_27 (and_27_out, not_36_out, in_1[1], not_37_out);
  and and_28 (and_28_out, in_1[2], not_38_out, in_1[0]);
  and and_29 (and_29_out, in_1[3], not_39_out, not_40_out);
  and and_30 (and_30_out, in_1[3], in_1[2], in_1[0]);
  and and_31 (and_31_out, not_41_out, not_42_out);
  and and_32 (and_32_out, in_1[2], in_1[1]);
  and and_33 (and_33_out, in_1[3], not_43_out);
  or or_1 (o8, and_1_out, and_2_out);
  or or_2 (o1, and_3_out, and_4_out, and_5_out, and_6_out, and_7_out);
  or or_3 (o2, and_8_out, and_9_out, and_10_out, and_11_out, and_12_out, and_13_out);
  or or_4 (o3, not_44_out, and_14_out, and_15_out, and_16_out, and_17_out);
  or or_5 (o4, and_18_out, and_19_out, and_20_out, and_21_out);
  or or_6 (o5, and_22_out, and_23_out, and_24_out);
  or or_7 (o6, and_25_out, and_26_out, and_27_out, and_28_out, and_29_out, and_30_out);
  or or_8 (o7, and_31_out, in_1[0], and_32_out, and_33_out);
endmodule

module anticlicker (
  input  in_1,
  input  in_2,
  input  in_3,
  input  in_4,
  input  in_5,
  output out_6
);

  wire not_1_out, or_1_out;

  or or_1 (or_1_out, in_2, in_3, in_4, in_5);
  D_Flip_Flop d_ff_1 (.clk(or_1_out), .D(1'b1), .Q(out_6), .reset(not_1_out));  // open: Qn, preset, en
  not not_1 (not_1_out, in_1);
endmodule

module anti_cheat (
  input  in_1,
  input  in_2,
  output out_3
);

  wire counter_1_q, not_1_out;

  not not_1 (not_1_out, in_1);
  Counter #(.width(1), .max('h1)) counter_1 (.Q(counter_1_q), .clk(in_1), .clr(in_2));  // open: load, D, count, carry
  and and_1 (out_3, not_1_out, counter_1_q, counter_1_q);
endmodule

module anti_cheat_2 (
  input  i1,
  input  i2,
  input  i3,
  input  i4,
  output o1
);

  wire and_1_out, and_2_out, and_3_out, and_4_out, and_5_out, and_6_out;

  and and_1 (and_1_out, i3, i4);
  and and_2 (and_2_out, i2, i4);
  and and_3 (and_3_out, i2, i3);
  and and_4 (and_4_out, i1, i4);
  and and_5 (and_5_out, i1, i3);
  and and_6 (and_6_out, i1, i2);
  or or_1 (o1, and_1_out, and_2_out, and_3_out, and_4_out, and_5_out, and_6_out);
endmodule
